// Logisim project alu.circ as structural Verilog: 8 circuits, main circuit main
module main (
);

  wire clock_1_out, processor_1_mrw, processor_1_msync;
  wire [6:0] processor_1_addressout;
  wire [13:0] ram_1_data;

  processor processor_1 (
    .Clock(clock_1_out), .DataIn(ram_1_data), .AddressOut(processor_1_addressout), .MSync(processor_1_msync),
    .MRW(processor_1_mrw));
  Clock #(.highDuration(1), .lowDuration(1)) clock_1 (.out(clock_1_out));
  RAM #(.addrWidth(7), .dataWidth(14), .bus("combined")) ram_1 (
    .addr(processor_1_addressout), .data(ram_1_data), .clk(processor_1_msync), .ld(processor_1_mrw));  // open: sel, clr

  // Notes on the sheet:
  //   Data
  //   Address
endmodule

module aluReloaded (
  input  [7:0] A,
  input  [7:0] B,
  input  [7:0] C,
  input  [7:0] D,
  input  ALUsum,
  input  [1:0] ALUtoEF,
  output [7:0] F,
  output [7:0] E
);

  wire [7:0] adder_1_out, adder_2_out, multiplexer_1_out, multiplexer_2_out;

  Multiplexer #(.select(1), .width(8)) multiplexer_1 (
    .in0(A), .in1(adder_1_out), .out(multiplexer_1_out), .sel(ALUsum));
  Multiplexer #(.select(1), .width(8)) multiplexer_2 (
    .in0(B), .in1(adder_2_out), .out(multiplexer_2_out), .sel(ALUsum));
  Adder #(.width(8)) adder_1 (.a(multiplexer_1_out), .b(multiplexer_2_out), .out(adder_1_out));  // open: cin, cout
  Adder #(.width(8)) adder_2 (.a(C), .b(D), .out(adder_2_out));  // open: cin, cout
  assign F = ALUtoEF[0] ? adder_2_out : 8'bz;  // Controlled_Buffer controlled_buffer_1
  assign E = ALUtoEF[1] ? adder_1_out : 8'bz;  // Controlled_Buffer controlled_buffer_2
endmodule

module processor (
  input  [13:0] DataIn,
  input  Clock,
  output [6:0] AddressOut,
  output MSync,
  output MRW
);

  wire undriven_5, undriven_7;
  wire [1:0] undriven_3, undriven_9;
  wire [3:0] undriven_8;
  wire [6:0] undriven_4;
  wire [7:0] alureloaded_1_e, alureloaded_1_f, registers_1_a, registers_1_b, registers_1_c, registers_1_d,
       undriven;
  wire [11:0] undriven_2;
  wire [13:0] undriven_6;

  registers registers_1 (
    .E(alureloaded_1_e), .F(alureloaded_1_f), .InSel_s_E_s_F(undriven), .OutSel_ABCD(undriven_2),
    .D(registers_1_d), .C(registers_1_c), .B(registers_1_b), .A(registers_1_a));
  aluReloaded alureloaded_1 (
    .F(alureloaded_1_f), .E(alureloaded_1_e), .ALUsum(undriven_7), .ALUtoEF(undriven_3), .A(registers_1_a),
    .B(registers_1_b), .C(registers_1_c), .D(registers_1_d));
  ProcessorRegisters processorregisters_1 (
    .Jump(1'b0), .Address(undriven_4), .MemAdd(undriven_5), .MBRIn(DataIn), .IRIn(undriven_6),
    .RegIn_PC_MAR_MBR_IR(undriven_8), .RegOut_MAR_MBR(undriven_9), .MARout(AddressOut), .MBRout(DataIn));  // open: IRout

  // Notes on the sheet:
  //   F-E
  //   A-B-C-D
  //   Data
  //   Address
endmodule

module registers (
  input  [7:0] E,
  input  [7:0] F,
  input  [7:0] InSel_s_E_s_F,
  input  [11:0] OutSel_ABCD,
  output [7:0] D,
  output [7:0] C,
  output [7:0] B,
  output [7:0] A
);

  wire regselector_1__0, regselector_1__1, regselector_1__2, regselector_1__3, regselector_1__4,
       regselector_1__5, regselector_1__6, regselector_1__7;
  wire [7:0] busselector_1__0, busselector_1__1, busselector_1__2, busselector_1__3, busselector_1__4,
       busselector_1__5, busselector_1__6, busselector_1__7, register_1_q, register_2_q, register_3_q,
       register_4_q, register_5_q, register_6_q, register_7_q, register_8_q;

  BusSelector busselector_1 (
    .E(E), .F(F), .fromE(InSel_s_E_s_F[2:0]), .fromF(InSel_s_E_s_F[6:4]), ._0(busselector_1__0),
    ._1(busselector_1__1), ._2(busselector_1__2), ._3(busselector_1__3), ._4(busselector_1__4),
    ._5(busselector_1__5), ._6(busselector_1__6), ._7(busselector_1__7));
  Register #(.width(8), .trigger("rising")) register_1 (
    .D(busselector_1__0), .Q(register_1_q), .clk(regselector_1__0));  // open: en, clr
  Register #(.width(8), .trigger("rising")) register_2 (
    .D(busselector_1__1), .Q(register_2_q), .clk(regselector_1__1));  // open: en, clr
  Register #(.width(8), .trigger("rising")) register_3 (
    .D(busselector_1__2), .Q(register_3_q), .clk(regselector_1__2));  // open: en, clr
  Register #(.width(8), .trigger("rising")) register_4 (
    .D(busselector_1__3), .Q(register_4_q), .clk(regselector_1__3));  // open: en, clr
  Register #(.width(8), .trigger("rising")) register_5 (
    .D(busselector_1__4), .Q(register_5_q), .clk(regselector_1__4));  // open: en, clr
  Register #(.width(8), .trigger("rising")) register_6 (
    .D(busselector_1__5), .Q(register_6_q), .clk(regselector_1__5));  // open: en, clr
  Register #(.width(8), .trigger("rising")) register_7 (
    .D(busselector_1__6), .Q(register_7_q), .clk(regselector_1__6));  // open: en, clr
  Register #(.width(8), .trigger("rising")) register_8 (
    .D(busselector_1__7), .Q(register_8_q), .clk(regselector_1__7));  // open: en, clr
  RegSelector regselector_1 (
    .FirstRegSel(InSel_s_E_s_F[7]), .FirstReg(InSel_s_E_s_F[6:4]), .SecondRegSel(InSel_s_E_s_F[3]),
    .SecondReg(InSel_s_E_s_F[2:0]), ._7(regselector_1__7), ._6(regselector_1__6), ._5(regselector_1__5),
    ._4(regselector_1__4), ._3(regselector_1__3), ._2(regselector_1__2), ._1(regselector_1__1),
    ._0(regselector_1__0));
  OutBusSel outbussel_1 (
    ._0(register_1_q), ._1(register_2_q), ._2(register_3_q), ._3(register_4_q), ._4(register_5_q),
    ._5(register_6_q), ._6(register_7_q), ._7(register_8_q), .OutSel_ABCD(OutSel_ABCD), .D(D), .C(C), .B(B),
    .A(A));
endmodule

module RegSelector (
  input  FirstRegSel,
  input  [2:0] FirstReg,
  input  SecondRegSel,
  input  [2:0] SecondReg,
  output _7,
  output _6,
  output _5,
  output _4,
  output _3,
  output _2,
  output _1,
  output _0
);

  wire and_1_out, and_2_out, and_3_out, and_4_out, and_5_out, and_6_out, and_7_out, and_8_out, and_9_out,
       and_10_out, and_11_out, and_12_out, and_13_out, and_14_out, and_15_out, and_16_out, decoder_1_out0,
       decoder_1_out1, decoder_1_out2, decoder_1_out3, decoder_1_out4, decoder_1_out5, decoder_1_out6,
       decoder_1_out7, decoder_2_out0, decoder_2_out1, decoder_2_out2, decoder_2_out3, decoder_2_out4,
       decoder_2_out5, decoder_2_out6, decoder_2_out7;

  Decoder #(.select(3), .tristate("false")) decoder_1 (
    .out0(decoder_1_out0), .out1(decoder_1_out1), .out2(decoder_1_out2), .out3(decoder_1_out3),
    .out4(decoder_1_out4), .out5(decoder_1_out5), .out6(decoder_1_out6), .out7(decoder_1_out7), .sel(FirstReg));
  or or_1 (_7, and_8_out, and_9_out);
  or or_2 (_6, and_7_out, and_12_out);
  and and_1 (and_1_out, decoder_1_out0, FirstRegSel);
  and and_2 (and_2_out, decoder_1_out1, FirstRegSel);
  and and_3 (and_3_out, decoder_1_out2, FirstRegSel);
  and and_4 (and_4_out, decoder_1_out3, FirstRegSel);
  and and_5 (and_5_out, decoder_1_out4, FirstRegSel);
  and and_6 (and_6_out, decoder_1_out5, FirstRegSel);
  and and_7 (and_7_out, decoder_1_out6, FirstRegSel);
  and and_8 (and_8_out, decoder_1_out7, FirstRegSel);
  and and_9 (and_9_out, SecondRegSel, decoder_2_out7);
  Decoder #(.select(3), .tristate("false")) decoder_2 (
    .out0(decoder_2_out0), .out1(decoder_2_out1), .out2(decoder_2_out2), .out3(decoder_2_out3),
    .out4(decoder_2_out4), .out5(decoder_2_out5), .out6(decoder_2_out6), .out7(decoder_2_out7),
    .sel(SecondReg));
  or or_3 (_4, and_5_out, and_10_out);
  or or_4 (_5, and_6_out, and_11_out);
  and and_10 (and_10_out, SecondRegSel, decoder_2_out4);
  and and_11 (and_11_out, SecondRegSel, decoder_2_out5);
  and and_12 (and_12_out, SecondRegSel, decoder_2_out6);
  or or_5 (_1, and_2_out, and_15_out);
  or or_6 (_2, and_3_out, and_13_out);
  or or_7 (_3, and_4_out, and_14_out);
  and and_13 (and_13_out, SecondRegSel, decoder_2_out2);
  and and_14 (and_14_out, SecondRegSel, decoder_2_out3);
  and and_15 (and_15_out, SecondRegSel, decoder_2_out1);
  or or_8 (_0, and_1_out, and_16_out);
  and and_16 (and_16_out, SecondRegSel, decoder_2_out0);
endmodule

module BusSelector (
  input  [7:0] E,
  input  [7:0] F,
  input  [2:0] fromE,
  input  [2:0] fromF,
  output [7:0] _0,
  output [7:0] _1,
  output [7:0] _2,
  output [7:0] _3,
  output [7:0] _4,
  output [7:0] _5,
  output [7:0] _6,
  output [7:0] _7
);

  Demultiplexer #(.select(3), .width(8), .tristate("true")) demultiplexer_1 (
    .out0(_0), .out1(_1), .out2(_2), .out3(_3), .out4(_4), .out5(_5), .out6(_6), .out7(_7), .in(E),
    .sel(fromE));
  Demultiplexer #(.select(3), .width(8), .tristate("true")) demultiplexer_2 (
    .out0(_0), .out1(_1), .out2(_2), .out3(_3), .out4(_4), .out5(_5), .out6(_6), .out7(_7), .in(F),
    .sel(fromF));
endmodule

module OutBusSel (
  input  [7:0] _0,
  input  [7:0] _1,
  input  [7:0] _2,
  input  [7:0] _3,
  input  [7:0] _4,
  input  [7:0] _5,
  input  [7:0] _6,
  input  [7:0] _7,
  input  [11:0] OutSel_ABCD,
  output [7:0] D,
  output [7:0] C,
  output [7:0] B,
  output [7:0] A
);

  Multiplexer #(.select(3), .width(8)) multiplexer_1 (
    .in0(_0), .in1(_1), .in2(_2), .in3(_3), .in4(_4), .in5(_5), .in6(_6), .in7(_7), .out(D),
    .sel(OutSel_ABCD[11:9]));
  Multiplexer #(.select(3), .width(8)) multiplexer_2 (
    .in0(_0), .in1(_1), .in2(_2), .in3(_3), .in4(_4), .in5(_5), .in6(_6), .in7(_7), .out(C),
    .sel(OutSel_ABCD[8:6]));
  Multiplexer #(.select(3), .width(8)) multiplexer_3 (
    .in0(_0), .in1(_1), .in2(_2), .in3(_3), .in4(_4), .in5(_5), .in6(_6), .in7(_7), .out(B),
    .sel(OutSel_ABCD[5:3]));
  Multiplexer #(.select(3), .width(8)) multiplexer_4 (
    .in0(_0), .in1(_1), .in2(_2), .in3(_3), .in4(_4), .in5(_5), .in6(_6), .in7(_7), .out(A),
    .sel(OutSel_ABCD[2:0]));
endmodule

module ProcessorRegisters (
  input  Jump,
  input  [6:0] Address,
  input  MemAdd,
  input  [13:0] MBRIn,
  input  [13:0] IRIn,
  input  [3:0] RegIn_PC_MAR_MBR_IR,
  input  [1:0] RegOut_MAR_MBR,
  output [6:0] MARout,
  output [13:0] MBRout,
  output [13:0] IRout
);

  wire [6:0] adder_1_out, MAR_q, multiplexer_1_out, multiplexer_2_out, PC_q;
  wire [13:0] MBR_q;

  Adder #(.width(7)) adder_1 (.a(PC_q), .b(7'b0000001), .out(adder_1_out));  // open: cin, cout
  Multiplexer #(.select(1), .width(7)) multiplexer_1 (
    .in0(adder_1_out), .in1(Address), .out(multiplexer_1_out), .sel(Jump));
  Register #(.width(7), .trigger("rising")) PC (
    .D(multiplexer_1_out), .Q(PC_q), .clk(RegIn_PC_MAR_MBR_IR[3]));  // open: en, clr
  Multiplexer #(.select(1), .width(7)) multiplexer_2 (.in0(PC_q), .in1(Address), .out(multiplexer_2_out), .sel(MemAdd));
  Register #(.width(7), .trigger("rising")) MAR (
    .D(multiplexer_2_out), .Q(MAR_q), .clk(RegIn_PC_MAR_MBR_IR[2]));  // open: en, clr
  Register #(.width(14), .trigger("rising")) MBR (.D(MBRIn), .Q(MBR_q), .clk(RegIn_PC_MAR_MBR_IR[1]));  // open: en, clr
  Register #(.width(14), .trigger("rising")) IR (.D(IRIn), .Q(IRout), .clk(RegIn_PC_MAR_MBR_IR[0]));  // open: en, clr
  assign MARout = RegOut_MAR_MBR[1] ? MAR_q : 7'bz;  // Controlled_Buffer controlled_buffer_1
  assign MBRout = RegOut_MAR_MBR[0] ? MBR_q : 14'bz;  // Controlled_Buffer controlled_buffer_2
endmodule
