// Logisim project not_working.circ as structural Verilog: 5 circuits, main circuit Parcial 2
module Parcial_2 (
  input  Reset
);

  wire adder_2_cout, uc_1_hin, uc_1_hout, uc_1_jin, uc_1_jout, uc_1_memrw, uc_1_pcin, uc_1_selbusc,
       uc_1_selbusdir, uc_1_sync;
  wire [3:0] adder_1_out, multiplexer_2_out, register_1_q, uc_1_posmemoria;
  wire [7:0] adder_2_out, controlled_buffer_1_out, multiplexer_1_out, register_2_q, register_3_q;

  Multiplexer #(.select(1), .width(8)) multiplexer_1 (
    .in0(adder_2_out), .in1(controlled_buffer_1_out), .out(multiplexer_1_out), .sel(uc_1_selbusc));
  Register #(.width(4), .trigger("rising")) register_1 (
    .D(adder_1_out), .Q(register_1_q), .clk(uc_1_pcin), .clr(Reset));  // open: en
  Register #(.width(8), .trigger("rising")) register_2 (
    .D(multiplexer_1_out), .Q(register_2_q), .clk(uc_1_hin));  // open: en, clr
  Register #(.width(8), .trigger("rising")) register_3 (
    .D(multiplexer_1_out), .Q(register_3_q), .clk(uc_1_jin), .clr(Reset));  // open: en
  Adder #(.width(4)) adder_1 (.a(4'b0001), .b(register_1_q), .out(adder_1_out));  // open: cin, cout
  Adder #(.width(8)) adder_2 (.a(register_2_q), .b(register_3_q), .out(adder_2_out), .cout(adder_2_cout));  // open: cin
  UC uc_1 (
    .PCin(uc_1_pcin), .Hin(uc_1_hin), .Jin(uc_1_jin), .SelBusC(uc_1_selbusc), .PosMemoria(uc_1_posmemoria),
    .IR(controlled_buffer_1_out), .SelBusDir(uc_1_selbusdir), .MemRW(uc_1_memrw), .Hout(uc_1_hout),
    .Jout(uc_1_jout), .sync(uc_1_sync));
  assign controlled_buffer_1_out = uc_1_hout ? register_2_q : 8'bz;  // Controlled_Buffer controlled_buffer_1
  assign controlled_buffer_1_out = uc_1_jout ? register_3_q : 8'bz;  // Controlled_Buffer controlled_buffer_2
  Multiplexer #(.select(1), .width(4)) multiplexer_2 (
    .in0(register_1_q), .in1(uc_1_posmemoria), .out(multiplexer_2_out), .sel(uc_1_selbusdir));
  RAM #(.addrWidth(4), .dataWidth(8), .bus("combined")) ram_1 (
    .addr(multiplexer_2_out), .data(controlled_buffer_1_out), .clk(uc_1_sync), .ld(uc_1_memrw));  // open: sel, clr

  // Notes on the sheet:
  //   Bus C
  //   PC
  //   H
  //   J
  //   Bus A
  //   Bus B
  //   Incrementador de PC
  //   PCin
  //   Hin
  //   Jin
  //   SelBusC
  //   ALU
  //   C
  //   V
  //   N
  //   PosMemoria
  //   IR
  //   UC
  //   Hout
  //   Jout
  //   Z
  //   Bus de direcciones
  //   SelBusDir
  //   MemRW
  //   Bus de datos
endmodule

module UC (
  input  [7:0] IR,
  output [3:0] PosMemoria,
  output PCin,
  output SelBusDir,
  output Hin,
  output MemRW,
  output Jin,
  output Hout,
  output SelBusC,
  output Jout,
  output sync
);

  wire clock_1_out;
  wire [1:0] rom_1_data;
  wire [3:0] register_1_q;
  wire [4:0] adder_1_out, multiplexer_1_out, register_2_q;
  wire [9:2] rom_1_data_2;

  Adder #(.width(5)) adder_1 (.a(register_2_q), .b(5'b00001), .out(adder_1_out));  // open: cin, cout
  Multiplexer #(.select(2), .width(5)) multiplexer_1 (
    .in0(adder_1_out), .in1({1'b1, register_1_q[3:2], 2'b00}), .in2({5{1'b0}}), .out(multiplexer_1_out),
    .sel(rom_1_data));  // open: in3
  Register #(.width(8), .trigger("high")) register_1 (
    .D(IR), .Q({register_1_q, PosMemoria}), .clk(rom_1_data_2[9]));  // open: en, clr
  Register #(.width(5), .trigger("rising")) register_2 (
    .D(multiplexer_1_out), .Q(register_2_q), .clk(clock_1_out));  // open: en, clr
  Clock #(.highDuration(1), .lowDuration(1)) clock_1 (.out(clock_1_out));
  ROM #(.addrWidth(5), .dataWidth(10)) rom_1 (
    .addr(register_2_q),
    .data({rom_1_data_2[9], PCin, SelBusDir, SelBusC, MemRW, sync, rom_1_data_2[3:2], rom_1_data}));  // open: sel
  regDecode regdecode_1 (.in_1(register_1_q[1]), .in_2(rom_1_data_2[3]), .H(Hin), .J(Jin));
  regDecode regdecode_2 (.in_1(register_1_q[1]), .in_2(rom_1_data_2[2]), .H(Hout), .J(Jout));

  // Notes on the sheet:
  //   contents of rom_1 (hex, n*v repeats v):
  //   230 101 14*0 f0 fa 0 0 84 96 0 0 a
endmodule

module regDecode (
  input  in_1,
  input  in_2,
  output H,
  output J
);

  wire decoder_1_out0, decoder_1_out1;

  Decoder #(.select(1), .tristate("false")) decoder_1 (.out0(decoder_1_out0), .out1(decoder_1_out1), .sel(in_1));
  and and_1 (H, in_2, decoder_1_out0);
  and and_2 (J, decoder_1_out1, in_2);
endmodule

module ALUreloaded (
  input  [7:0] DataIn,
  input  resetANDacum,
  output [7:0] SUMA,
  output [7:0] aMAR
);

  wire comparator_1_p2, comparator_1_p3, not_1_out, selreg_1__0, selreg_1__1, selreg_1__2, selreg_1__3,
       selreg_1__4, selreg_1__5, selreg_1__6, selreg_1__7, undriven_2;
  wire [7:0] adder_1_out, adder_2_out, adder_3_out, adder_4_out, adder_5_out, adder_6_out, adder_7_out,
       adder_8_out, adder_9_out, controlled_buffer_1_out, demultiplexer_1_out0, demultiplexer_1_out1,
       demultiplexer_1_out2, demultiplexer_1_out3, demultiplexer_1_out4, demultiplexer_1_out5,
       demultiplexer_1_out6, demultiplexer_1_out7, register_1_q, register_2_q, register_3_q, register_4_q,
       register_5_q, register_6_q, register_7_q, register_8_q, undriven;

  Demultiplexer #(.select(3), .width(8), .tristate("false")) demultiplexer_1 (
    .out0(demultiplexer_1_out0), .out1(demultiplexer_1_out1), .out2(demultiplexer_1_out2),
    .out3(demultiplexer_1_out3), .out4(demultiplexer_1_out4), .out5(demultiplexer_1_out5),
    .out6(demultiplexer_1_out6), .out7(demultiplexer_1_out7), .in(DataIn), .sel(aMAR[2:0]));
  selReg selreg_1 (
    .SecondReg(aMAR[2:0]), ._0(selreg_1__0), ._1(selreg_1__1), ._2(selreg_1__2), ._3(selreg_1__3),
    ._4(selreg_1__4), ._5(selreg_1__5), ._6(selreg_1__6), ._7(selreg_1__7));
  Register #(.width(8), .trigger("high")) register_1 (
    .D(demultiplexer_1_out0), .Q(register_1_q), .clk(selreg_1__0), .clr(resetANDacum));  // open: en
  Register #(.width(8), .trigger("high")) register_2 (
    .D(demultiplexer_1_out1), .Q(register_2_q), .clk(selreg_1__1), .clr(resetANDacum));  // open: en
  Register #(.width(8), .trigger("high")) register_3 (
    .D(demultiplexer_1_out2), .Q(register_3_q), .clk(selreg_1__2), .clr(resetANDacum));  // open: en
  Register #(.width(8), .trigger("high")) register_4 (
    .D(demultiplexer_1_out3), .Q(register_4_q), .clk(selreg_1__3), .clr(resetANDacum));  // open: en
  Register #(.width(8), .trigger("high")) register_5 (
    .D(demultiplexer_1_out4), .Q(register_5_q), .clk(selreg_1__4), .clr(resetANDacum));  // open: en
  Register #(.width(8), .trigger("high")) register_6 (
    .D(demultiplexer_1_out5), .Q(register_6_q), .clk(selreg_1__5), .clr(resetANDacum));  // open: en
  Register #(.width(8), .trigger("high")) register_7 (
    .D(demultiplexer_1_out6), .Q(register_7_q), .clk(selreg_1__6), .clr(resetANDacum));  // open: en
  Register #(.width(8), .trigger("high")) register_8 (
    .D(demultiplexer_1_out7), .Q(register_8_q), .clk(selreg_1__7), .clr(resetANDacum));  // open: en
  Adder #(.width(8)) adder_1 (.a(register_1_q), .b(register_2_q), .out(adder_1_out));  // open: cin, cout
  Adder #(.width(8)) adder_2 (.a(register_3_q), .b(register_4_q), .out(adder_2_out));  // open: cin, cout
  Adder #(.width(8)) adder_3 (.a(register_5_q), .b(register_6_q), .out(adder_3_out));  // open: cin, cout
  Adder #(.width(8)) adder_4 (.a(register_7_q), .b(register_8_q), .out(adder_4_out));  // open: cin, cout
  Register #(.width(8), .trigger("rising")) register_9 (.D(undriven), .clk(undriven_2));  // open: en, Q, clr
  Adder #(.width(8)) adder_5 (.a(adder_1_out), .b(adder_2_out), .out(adder_5_out));  // open: cin, cout
  Adder #(.width(8)) adder_6 (.a(adder_5_out), .b(adder_7_out), .out(adder_6_out));  // open: cin, cout
  Adder #(.width(8)) adder_7 (.a(adder_3_out), .b(adder_4_out), .out(adder_7_out));  // open: cin, cout
  assign controlled_buffer_1_out = not_1_out ? adder_6_out : 8'bz;  // Controlled_Buffer controlled_buffer_1
  not not_1 (not_1_out, resetANDacum);
  // Comparator #(.width(1), .mode("twosComplement")) comparator_1: pin names not known; wires that end beside it: aMAR, comparator_1_p2, comparator_1_p3
  Register #(.width(8), .trigger("rising")) acum (.D(adder_8_out), .Q(SUMA), .clk(resetANDacum));  // open: en, clr
  Adder #(.width(8)) adder_8 (.a(SUMA), .b(controlled_buffer_1_out), .out(adder_8_out));  // open: cin, cout
  Adder #(.width(8)) adder_9 (.a(8'h1), .b(aMAR), .out(adder_9_out));  // open: cin, cout
  Register #(.width(8), .trigger("rising")) register_10 (
    .D(adder_9_out), .Q(aMAR), .clk(comparator_1_p3));  // open: en, clr
  Controlled_Buffer #(.width(1)) controlled_buffer_2 ();  // open: in, out, en
endmodule

module selReg (
  input  [2:0] SecondReg,
  output _0,
  output _1,
  output _2,
  output _3,
  output _4,
  output _5,
  output _6,
  output _7
);

  Decoder #(.select(3), .tristate("false")) decoder_1 (
    .out0(_0), .out1(_1), .out2(_2), .out3(_3), .out4(_4), .out5(_5), .out6(_6), .out7(_7), .sel(SecondReg));
endmodule
