// Logisim project procesador_final.circ as structural Verilog: 11 circuits, main circuit main
module main (
);

  wire clock_1_out, processor_1_mrw, processor_1_msync;
  wire [6:0] processor_1_addressout;
  wire [15:0] ram_1_data;

  processor processor_1 (
    .Clock(clock_1_out), .DataIn(ram_1_data), .AddressOut(processor_1_addressout), .MRW(processor_1_mrw),
    .MSync(processor_1_msync));
  Clock #(.highDuration(1), .lowDuration(1)) clock_1 (.out(clock_1_out));
  // Probe on processor_1_addressout
  RAM #(.addrWidth(7), .dataWidth(16), .bus("combined")) ram_1 (
    .addr(processor_1_addressout), .data(ram_1_data), .clk(processor_1_msync), .ld(processor_1_mrw));  // open: sel, clr

  // Notes on the sheet:
  //   Data
  //   Address
  //   This memory is disabled
endmodule

module processor (
  input  [15:0] DataIn,
  input  Clock,
  output [6:0] AddressOut,
  output MRW,
  output MSync
);

  wire clkswap_1_uc, clkswap_1_ucalu, controlu_1_changeuc, controlu_1_memrw, controlu_1_msync,
       controlu_1_pcin, controlu_1_regin, controlu_1_regout1, controlu_1_regout2, controlu_1_selbackbus,
       controlu_1_selbusdir, controlualu_1_acum, controlualu_1_cut, controlualu_1_memrw, controlualu_1_msync,
       controlualu_1_regin1, controlualu_1_regin2, controlualu_1_resetall, controlualu_1_resetregs,
       controlualu_1_stop, decoder_1_out0, decoder_1_out1, not_1_out, undriven, undriven_2;
  wire [2:0] controlu_1_reg1, controlu_1_reg2;
  wire [6:0] controlled_buffer_1_out, controlu_1_posmemoria, controlualu_1_posmemoria, multiplexer_2_out,
       pc_1_dir;
  wire [7:0] registers_1_vectorsize;
  wire [15:0] alu_1_sum, multiplexer_1_out, registers_1_outbus, registers_1_outbus2;

  Multiplexer #(.select(1), .width(16)) multiplexer_1 (
    .in0(registers_1_outbus), .in1(alu_1_sum), .out(multiplexer_1_out), .sel(controlu_1_selbackbus));
  registers registers_1 (
    .InBuff(multiplexer_1_out), .reset(undriven), .regSelIn(controlu_1_regin), .regIn(controlu_1_reg2),
    .regOut(controlu_1_reg1), .regOutSel(controlu_1_regout1), .regOut2(controlu_1_reg2),
    .regOutsel2(controlu_1_regout2), .outBus2(registers_1_outbus2), .outBus(registers_1_outbus),
    .VectorSize(registers_1_vectorsize));
  ALU alu_1 (
    .Sum(alu_1_sum), .BusB(registers_1_outbus2), .BusA(registers_1_outbus), .Cut(controlualu_1_cut),
    .ValIn(registers_1_outbus), .Reg1(controlualu_1_regin1), .Reg2(controlualu_1_regin2),
    .Acum(controlualu_1_acum), .ResetAll(controlualu_1_resetall), .ResetRegs(controlualu_1_resetregs));
  ControlUALU controlualu_1 (
    .Cut(controlualu_1_cut), .Stop(controlualu_1_stop), .VectorSize(registers_1_vectorsize),
    .regIn2(controlualu_1_regin2), .regIn1(controlualu_1_regin1), .Acum(controlualu_1_acum),
    .CKL(clkswap_1_ucalu), .RST(undriven_2), .PosMemoria(controlualu_1_posmemoria),
    .ResetAll(controlualu_1_resetall), .ResetRegs(controlualu_1_resetregs), .MSync(controlualu_1_msync),
    .MemRW(controlualu_1_memrw));  // open: IniAdd
  PC pc_1 (.PCinc(controlu_1_pcin), .reset(undriven_2), .dir(pc_1_dir));
  Multiplexer #(.select(1), .width(7)) multiplexer_2 (
    .in0(pc_1_dir), .in1(controlu_1_posmemoria), .out(multiplexer_2_out), .sel(controlu_1_selbusdir));
  ControlU controlu_1 (
    .reg1(controlu_1_reg1), .reg2(controlu_1_reg2), .SelBackBus(controlu_1_selbackbus),
    .regIn(controlu_1_regin), .regOut1(controlu_1_regout1), .regOut2(controlu_1_regout2),
    .PosMemoria(controlu_1_posmemoria), .PCin(controlu_1_pcin), .SelBusDir(controlu_1_selbusdir),
    .CKL(clkswap_1_uc), .RST(undriven_2), .IR(registers_1_outbus), .MemRW(controlu_1_memrw),
    .MSync(controlu_1_msync), .ChangeUC(controlu_1_changeuc));
  CLKSwap clkswap_1 (
    .ChangeToUC(controlualu_1_stop), .Change(controlu_1_changeuc), .UCALU(clkswap_1_ucalu),
    .UC(clkswap_1_uc), .CLK(Clock));
  assign controlled_buffer_1_out = not_1_out ? multiplexer_2_out : 7'bz;  // Controlled_Buffer controlled_buffer_1
  not not_1 (not_1_out, controlu_1_changeuc);
  assign controlled_buffer_1_out = controlu_1_changeuc ? controlualu_1_posmemoria : 7'bz;  // Controlled_Buffer controlled_buffer_2
  assign MRW = decoder_1_out0 ? controlu_1_memrw : 1'bz;  // Controlled_Buffer controlled_buffer_3
  assign MSync = decoder_1_out0 ? controlu_1_msync : 1'bz;  // Controlled_Buffer controlled_buffer_4
  Decoder #(.select(1), .tristate("false")) decoder_1 (
    .out0(decoder_1_out0), .out1(decoder_1_out1), .sel(controlu_1_changeuc));
  assign MSync = decoder_1_out1 ? controlualu_1_msync : 1'bz;  // Controlled_Buffer controlled_buffer_5
  assign MRW = decoder_1_out1 ? controlualu_1_memrw : 1'bz;  // Controlled_Buffer controlled_buffer_6
  RAM #(.addrWidth(7), .dataWidth(16), .bus("combined")) ram_1 (
    .addr(controlled_buffer_1_out), .data(registers_1_outbus), .clk(MSync), .ld(MRW));  // open: sel, clr

  // Notes on the sheet:
  //   Data 2
  //   Data
  //   Address
endmodule

module registers (
  input  reset,
  input  [15:0] InBuff,
  input  [2:0] regOut,
  input  regOutSel,
  input  [2:0] regOut2,
  input  regOutsel2,
  input  regSelIn,
  input  [2:0] regIn,
  output [15:0] outBus2,
  output [15:0] outBus,
  output [7:0] VectorSize
);

  wire regselector_1__0, regselector_1__1, regselector_1__2, regselector_1__3, regselector_1__4,
       regselector_1__5, regselector_1__6, regselector_1__7;
  wire [15:0] register_1_q, register_2_q, register_3_q, register_4_q, register_5_q, register_6_q,
       register_7_q;
  wire [15:8] register_8_q;

  Register #(.width(16), .trigger("rising")) register_1 (
    .D(InBuff), .Q(register_1_q), .clk(regselector_1__0), .clr(reset));  // open: en
  Register #(.width(16), .trigger("rising")) register_2 (
    .D(InBuff), .Q(register_2_q), .clk(regselector_1__1), .clr(reset));  // open: en
  Register #(.width(16), .trigger("rising")) register_3 (
    .D(InBuff), .Q(register_3_q), .clk(regselector_1__2), .clr(reset));  // open: en
  Register #(.width(16), .trigger("rising")) register_4 (
    .D(InBuff), .Q(register_4_q), .clk(regselector_1__3), .clr(reset));  // open: en
  Register #(.width(16), .trigger("rising")) register_5 (
    .D(InBuff), .Q(register_5_q), .clk(regselector_1__4), .clr(reset));  // open: en
  Register #(.width(16), .trigger("rising")) register_6 (
    .D(InBuff), .Q(register_6_q), .clk(regselector_1__5), .clr(reset));  // open: en
  Register #(.width(16), .trigger("rising")) register_7 (
    .D(InBuff), .Q(register_7_q), .clk(regselector_1__6), .clr(reset));  // open: en
  Register #(.width(16), .trigger("rising")) register_8 (
    .D(InBuff), .Q({register_8_q, VectorSize}), .clk(regselector_1__7), .clr(reset));  // open: en
  RegSelector regselector_1 (
    .RegIn(regSelIn), .Reg(regIn), ._7(regselector_1__7), ._6(regselector_1__6), ._5(regselector_1__5),
    ._4(regselector_1__4), ._3(regselector_1__3), ._2(regselector_1__2), ._1(regselector_1__1),
    ._0(regselector_1__0));
  OutBusSel outbussel_1 (
    ._0(register_1_q), ._1(register_2_q), ._2(register_3_q), ._3(register_4_q), ._4(register_5_q),
    ._5(register_6_q), ._6(register_7_q), ._7({register_8_q, VectorSize}), .OutBus(regOut),
    .OutBus2(regOut2), .regOut(regOutSel), .regOut2(regOutsel2), .outBus2_2(outBus2), .outBus_2(outBus));
endmodule

module RegSelector (
  input  RegIn,
  input  [2:0] Reg,
  output _7,
  output _6,
  output _5,
  output _4,
  output _3,
  output _2,
  output _1,
  output _0
);

  wire decoder_1_out0, decoder_1_out1, decoder_1_out2, decoder_1_out3, decoder_1_out4, decoder_1_out5,
       decoder_1_out6, decoder_1_out7;

  Decoder #(.select(3), .tristate("false")) decoder_1 (
    .out0(decoder_1_out0), .out1(decoder_1_out1), .out2(decoder_1_out2), .out3(decoder_1_out3),
    .out4(decoder_1_out4), .out5(decoder_1_out5), .out6(decoder_1_out6), .out7(decoder_1_out7), .sel(Reg));
  and and_1 (_0, decoder_1_out0, RegIn);
  and and_2 (_1, decoder_1_out1, RegIn);
  and and_3 (_2, decoder_1_out2, RegIn);
  and and_4 (_3, decoder_1_out3, RegIn);
  and and_5 (_4, decoder_1_out4, RegIn);
  and and_6 (_5, decoder_1_out5, RegIn);
  and and_7 (_6, decoder_1_out6, RegIn);
  and and_8 (_7, decoder_1_out7, RegIn);
endmodule

module OutBusSel (
  input  [15:0] _0,
  input  [15:0] _1,
  input  [15:0] _2,
  input  [15:0] _3,
  input  [15:0] _4,
  input  [15:0] _5,
  input  [15:0] _6,
  input  [15:0] _7,
  input  [2:0] OutBus,
  input  [2:0] OutBus2,
  input  regOut,
  input  regOut2,
  output [15:0] outBus2_2,
  output [15:0] outBus_2
);

  wire [15:0] multiplexer_1_out, multiplexer_2_out;

  Multiplexer #(.select(3), .width(16)) multiplexer_1 (
    .in0(_0), .in1(_1), .in2(_2), .in3(_3), .in4(_4), .in5(_5), .in6(_6), .in7(_7), .out(multiplexer_1_out),
    .sel(OutBus));
  Multiplexer #(.select(3), .width(16)) multiplexer_2 (
    .in0(_0), .in1(_1), .in2(_2), .in3(_3), .in4(_4), .in5(_5), .in6(_6), .in7(_7), .out(multiplexer_2_out),
    .sel(OutBus2));
  assign outBus_2 = regOut ? multiplexer_1_out : 16'bz;  // Controlled_Buffer controlled_buffer_1
  assign outBus2_2 = regOut2 ? multiplexer_2_out : 16'bz;  // Controlled_Buffer controlled_buffer_2
endmodule

module ControlU (
  input  [15:0] IR,
  input  CKL,
  input  RST,
  output [6:0] PosMemoria,
  output PCin,
  output [2:0] reg1,
  output [2:0] reg2,
  output SelBusDir,
  output SelBackBus,
  output regIn,
  output regOut1,
  output regOut2,
  output MemRW,
  output MSync,
  output ChangeUC
);

  wire instrhijacker_1__1_reg_mem_0_mem_reg;
  wire [1:0] rom_1_data;
  wire [3:0] instrhijacker_1_opcode;
  wire [4:0] adder_1_out, multiplexer_1_out, register_2_q;
  wire [10:10] rom_1_data_2;
  wire [15:0] register_1_q;

  or or_1 (instrhijacker_1_opcode[3], instrhijacker_1__1_reg_mem_0_mem_reg, 1'b0);
  Register #(.width(16), .trigger("high")) register_1 (
    .D(IR), .Q(register_1_q), .clk(rom_1_data_2[10]), .clr(RST));  // open: en
  InstrHiJacker instrhijacker_1 (
    .in(register_1_q), .dirMem(PosMemoria), .opCode(instrhijacker_1_opcode[2:0]),
    ._1_reg_mem_0_mem_reg(instrhijacker_1__1_reg_mem_0_mem_reg), .reg1(reg1), .reg2(reg2), .SumV(ChangeUC));
  Adder #(.width(5)) adder_1 (.a(register_2_q), .b(5'b00001), .out(adder_1_out));  // open: cin, cout
  Multiplexer #(.select(2), .width(5)) multiplexer_1 (
    .in0(adder_1_out), .in1({1'b1, instrhijacker_1_opcode}), .in2({5{1'b0}}), .out(multiplexer_1_out),
    .sel(rom_1_data));  // open: in3
  Register #(.width(5), .trigger("rising")) register_2 (
    .D(multiplexer_1_out), .Q(register_2_q), .clk(CKL), .clr(RST));  // open: en
  ROM #(.addrWidth(5), .dataWidth(11)) rom_1 (
    .addr(register_2_q),
    .data({rom_1_data_2[10], PCin, SelBusDir, SelBackBus, regIn, regOut1, regOut2, MemRW, MSync, rom_1_data}));  // open: sel

  // Notes on the sheet:
  //   contents of rom_1 (hex, n*v repeats v):
  //   40c 201 14*0 10c 14e b0 c2 20 62 0 1 120 126 0 0 b0 c2
endmodule

module PC (
  input  PCinc,
  input  reset,
  output [6:0] dir
);

  wire [6:0] adder_1_out;

  Adder #(.width(7)) adder_1 (.a(dir), .b(7'b0000001), .out(adder_1_out));  // open: cin, cout
  Register #(.width(7), .trigger("rising")) PC (.D(adder_1_out), .Q(dir), .clk(PCinc), .clr(reset));  // open: en
endmodule

module InstrHiJacker (
  input  [15:0] in,
  output SumV,
  output [2:0] reg1,
  output [2:0] reg2,
  output [6:0] dirMem,
  output _1_reg_mem_0_mem_reg,
  output [2:0] opCode
);

  wire decoder_1_out0, decoder_1_out1, decoder_1_out2, not_1_out, or_2_out;
  wire [2:0] multiplexer_1_out;
  wire [10:7] controlled_buffer_1_out;

  Multiplexer #(.select(3), .width(3)) multiplexer_1 (
    .in0(3'b000), .in1(3'b011), .in2(3'b000), .in3(3'b001), .out(multiplexer_1_out), .sel(in[15:13]));  // open: in4, in5, in6, in7
  Decoder #(.select(3), .tristate("false")) decoder_1 (
    .out0(decoder_1_out0), .out1(decoder_1_out1), .out2(decoder_1_out2), .out3(SumV), .sel(in[15:13]));  // open: out4, out5, out6, out7
  Adder #(.width(3)) adder_1 (.a(multiplexer_1_out), .b(in[15:13]), .out(opCode));  // open: cin, cout
  assign {controlled_buffer_1_out, dirMem} = decoder_1_out0 ? in[12:2] : 11'bz;  // Controlled_Buffer controlled_buffer_1
  or or_1 (_1_reg_mem_0_mem_reg, controlled_buffer_1_out[7], SumV);
  or or_2 (or_2_out, decoder_1_out2, decoder_1_out1);
  assign {reg1, reg2} = or_2_out ? in[12:7] : 6'bz;  // Controlled_Buffer controlled_buffer_2
  assign reg1 = controlled_buffer_1_out[7] ? controlled_buffer_1_out[10:8] : 3'bz;  // Controlled_Buffer controlled_buffer_3
  not not_1 (not_1_out, controlled_buffer_1_out[7]);
  assign reg2 = not_1_out ? controlled_buffer_1_out[10:8] : 3'bz;  // Controlled_Buffer controlled_buffer_4
  assign dirMem = SumV ? in[8:2] : 7'bz;  // Controlled_Buffer controlled_buffer_5
endmodule

module ALU (
  input  Cut,
  input  [15:0] BusB,
  input  [15:0] BusA,
  input  Reg1,
  input  Reg2,
  input  Acum,
  input  ResetAll,
  input  ResetRegs,
  output [15:0] ValIn,
  output [15:0] Sum
);

  wire and_1_out, and_2_out, not_1_out, not_2_out, not_3_out, undriven;
  wire [7:0] Acum_q, adder_2_out, adder_3_out, adder_4_out, adder_5_out;
  wire [15:0] adder_1_out, controlled_buffer_3_out, controlled_buffer_5_out, register_1_q, register_2_q;

  Adder #(.width(16)) adder_1 (.a(BusA), .b(BusB), .out(adder_1_out));  // open: cin, cout
  assign Sum = not_1_out ? adder_1_out : 16'bz;  // Controlled_Buffer controlled_buffer_1
  not not_1 (not_1_out, undriven);
  assign Sum = undriven ? {{8{1'b0}}, Acum_q} : 16'bz;  // Controlled_Buffer controlled_buffer_2
  not not_2 (not_2_out, and_1_out);
  and and_1 (and_1_out, Cut, Reg1);
  not not_3 (not_3_out, and_2_out);
  and and_2 (and_2_out, Cut, Reg2);
  assign controlled_buffer_3_out = not_2_out ? ValIn : 16'bz;  // Controlled_Buffer controlled_buffer_3
  assign controlled_buffer_3_out = and_1_out ? {ValIn[15:8], {8{1'b0}}} : 16'bz;  // Controlled_Buffer controlled_buffer_4
  assign controlled_buffer_5_out = not_3_out ? ValIn : 16'bz;  // Controlled_Buffer controlled_buffer_5
  assign controlled_buffer_5_out = and_2_out ? {ValIn[15:8], {8{1'b0}}} : 16'bz;  // Controlled_Buffer controlled_buffer_6
  Register #(.width(16), .trigger("rising")) register_1 (
    .D(controlled_buffer_3_out), .Q(register_1_q), .clk(Reg1), .clr(ResetRegs));  // open: en
  Register #(.width(16), .trigger("rising")) register_2 (
    .D(controlled_buffer_5_out), .Q(register_2_q), .clk(Reg2), .clr(ResetRegs));  // open: en
  Adder #(.width(8)) adder_2 (.a(register_1_q[7:0]), .b(register_1_q[15:8]), .out(adder_2_out));  // open: cin, cout
  Adder #(.width(8)) adder_3 (.a(register_2_q[7:0]), .b(register_2_q[15:8]), .out(adder_3_out));  // open: cin, cout
  Adder #(.width(8)) adder_4 (.a(adder_2_out), .b(adder_3_out), .out(adder_4_out));  // open: cin, cout
  buf buffer_1 (ResetRegs, ResetAll);
  Adder #(.width(8)) adder_5 (.a(Acum_q), .b(adder_4_out), .out(adder_5_out));  // open: cin, cout
  Register #(.width(8), .trigger("rising")) u_Acum (
    .D(adder_5_out), .Q(Acum_q), .clk(Acum), .clr(ResetAll));  // open: en
endmodule

module ControlUALU (
  input  [6:0] IniAdd,
  input  [7:0] VectorSize,
  input  CKL,
  input  RST,
  output [6:0] PosMemoria,
  output Cut,
  output Stop,
  output Acum,
  output ResetAll,
  output ResetRegs,
  output regIn2,
  output regIn1,
  output MSync,
  output MemRW
);

  wire [1:0] or_1_out;
  wire [2:0] adder_2_out, multiplexer_2_out, register_1_q;
  wire [6:0] adder_1_out, multiplexer_1_out;
  wire [7:0] adder_3_out, Size_q, Tmp_q;
  wire [7:7] rom_1_data;

  Clock #(.highDuration(1), .lowDuration(1)) clock_1 ();  // open: out
  Adder #(.width(7)) adder_1 (.a(IniAdd), .b(7'b0000001), .out(adder_1_out));  // open: cin, cout
  Adder #(.width(3)) adder_2 (.a(register_1_q), .b(3'b001), .out(adder_2_out));  // open: cin, cout
  Register #(.width(7), .trigger("rising")) PosC (
    .D(multiplexer_1_out), .Q(IniAdd), .clk(rom_1_data[7]), .clr(RST));  // open: en
  Multiplexer #(.select(1), .width(7)) multiplexer_1 (
    .in0(adder_1_out), .in1(IniAdd), .out(multiplexer_1_out), .sel(CKL));
  Multiplexer #(.select(2), .width(3)) multiplexer_2 (
    .in0(adder_2_out), .in1(3'b000), .in2(3'b111), .in3(3'b111), .out(multiplexer_2_out), .sel(or_1_out));
  Register #(.width(3), .trigger("rising")) register_1 (
    .D(multiplexer_2_out), .Q(register_1_q), .clk(CKL), .clr(RST));  // open: en
  Adder #(.width(8)) adder_3 (.a(Tmp_q), .b(8'h2), .out(adder_3_out));  // open: cin, cout
  Register #(.width(8), .trigger("rising")) Tmp (
    .D(adder_3_out), .Q(Tmp_q), .clk(rom_1_data[7]), .clr(RST));  // open: en
  Register #(.width(8), .trigger("rising")) Size (.D(VectorSize), .Q(Size_q), .clk(CKL), .clr(RST));  // open: en
  ROM #(.addrWidth(3), .dataWidth(8)) rom_1 (
    .addr(register_1_q), .data({rom_1_data[7], MSync, regIn1, regIn2, ResetRegs, ResetAll, Acum, or_1_out[0]}));  // open: sel
  Comparator #(.width(8), .mode("twosComplement")) comparator_1 (
    .a(Tmp_q), .b(Size_q), .gt(Cut), .eq(Stop));  // open: lt
  or or_1 (or_1_out[1], Stop, Cut);

  assign MemRW = 1'b0;
  assign PosMemoria = IniAdd;

  // Notes on the sheet:
  //   contents of rom_1 (hex, n*v repeats v):
  //   40 60 d2 89 0 0 0 e
endmodule

module CLKSwap (
  input  ChangeToUC,
  input  Change,
  input  CLK,
  output UCALU,
  output UC
);

  wire and_1_out, d_ff_1_q, d_ff_1_qn, not_1_out;

  not not_1 (not_1_out, ChangeToUC);
  and and_1 (and_1_out, Change, not_1_out);
  D_Flip_Flop #(.trigger("rising")) d_ff_1 (
    .clk(CLK), .D(and_1_out), .Q(d_ff_1_q), .Qn(d_ff_1_qn));  // open: preset, en, reset
  assign UCALU = d_ff_1_q ? CLK : 1'bz;  // Controlled_Buffer controlled_buffer_1
  assign UC = d_ff_1_qn ? CLK : 1'bz;  // Controlled_Buffer controlled_buffer_2
endmodule
