// Logisim project working.circ as structural Verilog: 13 circuits, main circuit main
module main (
);

  wire clock_1_out, processor_1_mrw, processor_1_msync;
  wire [6:0] processor_1_addressout;
  wire [15:0] ram_1_data;

  processor processor_1 (
    .Clock(clock_1_out), .DataIn(ram_1_data), .AddressOut(processor_1_addressout), .MRW(processor_1_mrw),
    .MSync(processor_1_msync));
  Clock #(.highDuration(1), .lowDuration(1)) clock_1 (.out(clock_1_out));
  // Probe on processor_1_addressout
  RAM #(.addrWidth(7), .dataWidth(16), .bus("combined")) ram_1 (
    .addr(processor_1_addressout), .data(ram_1_data), .clk(processor_1_mrw), .ld(processor_1_msync));  // open: sel, clr

  // Notes on the sheet:
  //   Data
  //   Address
endmodule

module aluReloaded (
  input  [15:0] A,
  input  [15:0] B,
  input  [15:0] C,
  input  [15:0] D,
  input  [1:0] ALUtoEF,
  input  ALUsum,
  output [15:0] F,
  output [15:0] E
);

  wire [15:0] adder_1_out, adder_2_out, multiplexer_1_out, multiplexer_2_out;

  Multiplexer #(.select(1), .width(16)) multiplexer_1 (
    .in0(A), .in1(adder_1_out), .out(multiplexer_1_out), .sel(ALUsum));
  Multiplexer #(.select(1), .width(16)) multiplexer_2 (
    .in0(B), .in1(adder_2_out), .out(multiplexer_2_out), .sel(ALUsum));
  Adder #(.width(16)) adder_1 (.a(multiplexer_1_out), .b(multiplexer_2_out), .out(adder_1_out));  // open: cin, cout
  Adder #(.width(16)) adder_2 (.a(C), .b(D), .out(adder_2_out));  // open: cin, cout
  assign F = ALUtoEF[0] ? adder_2_out : 16'bz;  // Controlled_Buffer controlled_buffer_1
  assign E = ALUtoEF[1] ? adder_1_out : 16'bz;  // Controlled_Buffer controlled_buffer_2
endmodule

module processor (
  input  [15:0] DataIn,
  input  Clock,
  output [6:0] AddressOut,
  output MRW,
  output MSync
);

  wire controlu_1_alusum, controlu_1_memadd, controlu_1_regout, undriven;
  wire [1:0] controlu_1_alutoef, controlu_1_mar_mbr_out;
  wire [3:0] controlu_1_pc_mar_mbr_ir_in;
  wire [6:0] controlu_1_address;
  wire [7:0] controlu_1_in_se_sf;
  wire [11:0] controlu_1_abcd;
  wire [15:0] alureloaded_1_e, alureloaded_1_f, processorregisters_1_irout, registers_1_a, registers_1_b,
       registers_1_c, registers_1_d;

  registers registers_1 (
    .E(alureloaded_1_e), .F(alureloaded_1_f), .InSel_s_E_s_F(controlu_1_in_se_sf),
    .OutSel_ABCD(controlu_1_abcd), .reset(undriven), .D(registers_1_d), .C(registers_1_c), .B(registers_1_b),
    .A(registers_1_a));
  aluReloaded alureloaded_1 (
    .F(alureloaded_1_f), .E(alureloaded_1_e), .ALUtoEF(controlu_1_alutoef), .ALUsum(controlu_1_alusum),
    .A(registers_1_a), .B(registers_1_b), .C(registers_1_c), .D(registers_1_d));
  assign DataIn = controlu_1_regout ? registers_1_a : 16'bz;  // Controlled_Buffer controlled_buffer_1
  // Probe on alureloaded_1_e
  ProcessorRegisters processorregisters_1 (
    .Jump(1'b0), .Address(controlu_1_address), .MemAdd(controlu_1_memadd), .MBRIn(DataIn), .IRIn(DataIn),
    .\reg (undriven), .RegIn_PC_MAR_MBR_IR(controlu_1_pc_mar_mbr_ir_in),
    .RegOut_MAR_MBR(controlu_1_mar_mbr_out), .MARout(AddressOut), .MBRout(alureloaded_1_e),
    .IRout(processorregisters_1_irout));
  ControlU controlu_1 (
    .ABCD(controlu_1_abcd), .in_sE_sF(controlu_1_in_se_sf), .ALUsum(controlu_1_alusum),
    .AlUtoEF(controlu_1_alutoef), .regOut(controlu_1_regout), .ir(processorregisters_1_irout),
    .address(controlu_1_address), .memAdd(controlu_1_memadd), .PC_MAR_MBR_IR_in(controlu_1_pc_mar_mbr_ir_in),
    .MAR_MBR_out(controlu_1_mar_mbr_out), .reset(undriven), .clock(Clock), .MemRW(MRW), .sync(MSync));

  // Notes on the sheet:
  //   F-E
  //   A-B-C-D
  //   Data
  //   Address
endmodule

module registers (
  input  [15:0] E,
  input  [15:0] F,
  input  [7:0] InSel_s_E_s_F,
  input  [11:0] OutSel_ABCD,
  input  reset,
  output [15:0] D,
  output [15:0] C,
  output [15:0] B,
  output [15:0] A
);

  wire regselector_1__0, regselector_1__1, regselector_1__2, regselector_1__3, regselector_1__4,
       regselector_1__5, regselector_1__6, regselector_1__7;
  wire [15:0] busselector_1__0, busselector_1__1, busselector_1__2, busselector_1__3, busselector_1__4,
       busselector_1__5, busselector_1__6, busselector_1__7, register_1_q, register_2_q, register_3_q,
       register_4_q, register_5_q, register_6_q, register_7_q, register_8_q;

  BusSelector busselector_1 (
    .E(E), .F(F), .fromE(InSel_s_E_s_F[6:4]), .fromF(InSel_s_E_s_F[2:0]), ._0(busselector_1__0),
    ._1(busselector_1__1), ._2(busselector_1__2), ._3(busselector_1__3), ._4(busselector_1__4),
    ._5(busselector_1__5), ._6(busselector_1__6), ._7(busselector_1__7));
  Register #(.width(16), .trigger("rising")) register_1 (
    .D(busselector_1__0), .Q(register_1_q), .clk(regselector_1__0), .clr(reset));  // open: en
  Register #(.width(16), .trigger("rising")) register_2 (
    .D(busselector_1__1), .Q(register_2_q), .clk(regselector_1__1), .clr(reset));  // open: en
  Register #(.width(16), .trigger("rising")) register_3 (
    .D(busselector_1__2), .Q(register_3_q), .clk(regselector_1__2), .clr(reset));  // open: en
  Register #(.width(16), .trigger("rising")) register_4 (
    .D(busselector_1__3), .Q(register_4_q), .clk(regselector_1__3), .clr(reset));  // open: en
  Register #(.width(16), .trigger("rising")) register_5 (
    .D(busselector_1__4), .Q(register_5_q), .clk(regselector_1__4), .clr(reset));  // open: en
  Register #(.width(16), .trigger("rising")) register_6 (
    .D(busselector_1__5), .Q(register_6_q), .clk(regselector_1__5), .clr(reset));  // open: en
  Register #(.width(16), .trigger("rising")) register_7 (
    .D(busselector_1__6), .Q(register_7_q), .clk(regselector_1__6), .clr(reset));  // open: en
  Register #(.width(16), .trigger("rising")) register_8 (
    .D(busselector_1__7), .Q(register_8_q), .clk(regselector_1__7), .clr(reset));  // open: en
  RegSelector regselector_1 (
    .FirstRegSel(InSel_s_E_s_F[7]), .FirstReg(InSel_s_E_s_F[6:4]), .SecondRegSel(InSel_s_E_s_F[3]),
    .SecondReg(InSel_s_E_s_F[2:0]), ._7(regselector_1__7), ._6(regselector_1__6), ._5(regselector_1__5),
    ._4(regselector_1__4), ._3(regselector_1__3), ._2(regselector_1__2), ._1(regselector_1__1),
    ._0(regselector_1__0));
  OutBusSel outbussel_1 (
    ._0(register_1_q), ._1(register_2_q), ._2(register_3_q), ._3(register_4_q), ._4(register_5_q),
    ._5(register_6_q), ._6(register_7_q), ._7(register_8_q), .OutSel_ABCD(OutSel_ABCD), .D(D), .C(C), .B(B),
    .A(A));
endmodule

module RegSelector (
  input  FirstRegSel,
  input  [2:0] FirstReg,
  input  SecondRegSel,
  input  [2:0] SecondReg,
  output _7,
  output _6,
  output _5,
  output _4,
  output _3,
  output _2,
  output _1,
  output _0
);

  wire and_1_out, and_2_out, and_3_out, and_4_out, and_5_out, and_6_out, and_7_out, and_8_out, and_9_out,
       and_10_out, and_11_out, and_12_out, and_13_out, and_14_out, and_15_out, and_16_out, decoder_1_out0,
       decoder_1_out1, decoder_1_out2, decoder_1_out3, decoder_1_out4, decoder_1_out5, decoder_1_out6,
       decoder_1_out7, decoder_2_out0, decoder_2_out1, decoder_2_out2, decoder_2_out3, decoder_2_out4,
       decoder_2_out5, decoder_2_out6, decoder_2_out7;

  Decoder #(.select(3), .tristate("false")) decoder_1 (
    .out0(decoder_1_out0), .out1(decoder_1_out1), .out2(decoder_1_out2), .out3(decoder_1_out3),
    .out4(decoder_1_out4), .out5(decoder_1_out5), .out6(decoder_1_out6), .out7(decoder_1_out7), .sel(FirstReg));
  or or_1 (_6, and_7_out, and_10_out);
  or or_2 (_7, and_8_out, and_9_out);
  and and_1 (and_1_out, decoder_1_out0, FirstRegSel);
  and and_2 (and_2_out, decoder_1_out1, FirstRegSel);
  and and_3 (and_3_out, decoder_1_out2, FirstRegSel);
  and and_4 (and_4_out, decoder_1_out3, FirstRegSel);
  and and_5 (and_5_out, decoder_1_out4, FirstRegSel);
  and and_6 (and_6_out, decoder_1_out5, FirstRegSel);
  and and_7 (and_7_out, decoder_1_out6, FirstRegSel);
  and and_8 (and_8_out, decoder_1_out7, FirstRegSel);
  and and_9 (and_9_out, SecondRegSel, decoder_2_out7);
  Decoder #(.select(3), .tristate("false")) decoder_2 (
    .out0(decoder_2_out0), .out1(decoder_2_out1), .out2(decoder_2_out2), .out3(decoder_2_out3),
    .out4(decoder_2_out4), .out5(decoder_2_out5), .out6(decoder_2_out6), .out7(decoder_2_out7),
    .sel(SecondReg));
  or or_3 (_5, and_6_out, and_11_out);
  or or_4 (_4, and_5_out, and_12_out);
  and and_10 (and_10_out, SecondRegSel, decoder_2_out6);
  and and_11 (and_11_out, SecondRegSel, decoder_2_out5);
  and and_12 (and_12_out, SecondRegSel, decoder_2_out4);
  or or_5 (_3, and_4_out, and_15_out);
  or or_6 (_2, and_3_out, and_14_out);
  or or_7 (_1, and_2_out, and_13_out);
  and and_13 (and_13_out, SecondRegSel, decoder_2_out1);
  and and_14 (and_14_out, SecondRegSel, decoder_2_out2);
  and and_15 (and_15_out, SecondRegSel, decoder_2_out3);
  or or_8 (_0, and_1_out, and_16_out);
  and and_16 (and_16_out, SecondRegSel, decoder_2_out0);
endmodule

module BusSelector (
  input  [15:0] E,
  input  [15:0] F,
  input  [2:0] fromE,
  input  [2:0] fromF,
  output [15:0] _0,
  output [15:0] _1,
  output [15:0] _2,
  output [15:0] _3,
  output [15:0] _4,
  output [15:0] _5,
  output [15:0] _6,
  output [15:0] _7
);

  Demultiplexer #(.select(3), .width(16), .tristate("true")) demultiplexer_1 (
    .out0(_0), .out1(_1), .out2(_2), .out3(_3), .out4(_4), .out5(_5), .out6(_6), .out7(_7), .in(E),
    .sel(fromE));
  Demultiplexer #(.select(3), .width(16), .tristate("true")) demultiplexer_2 (
    .out0(_0), .out1(_1), .out2(_2), .out3(_3), .out4(_4), .out5(_5), .out6(_6), .out7(_7), .in(F),
    .sel(fromF));
endmodule

module OutBusSel (
  input  [15:0] _0,
  input  [15:0] _1,
  input  [15:0] _2,
  input  [15:0] _3,
  input  [15:0] _4,
  input  [15:0] _5,
  input  [15:0] _6,
  input  [15:0] _7,
  input  [11:0] OutSel_ABCD,
  output [15:0] D,
  output [15:0] C,
  output [15:0] B,
  output [15:0] A
);

  Multiplexer #(.select(3), .width(16)) multiplexer_1 (
    .in0(_0), .in1(_1), .in2(_2), .in3(_3), .in4(_4), .in5(_5), .in6(_6), .in7(_7), .out(D),
    .sel(OutSel_ABCD[2:0]));
  Multiplexer #(.select(3), .width(16)) multiplexer_2 (
    .in0(_0), .in1(_1), .in2(_2), .in3(_3), .in4(_4), .in5(_5), .in6(_6), .in7(_7), .out(C),
    .sel(OutSel_ABCD[5:3]));
  Multiplexer #(.select(3), .width(16)) multiplexer_3 (
    .in0(_0), .in1(_1), .in2(_2), .in3(_3), .in4(_4), .in5(_5), .in6(_6), .in7(_7), .out(B),
    .sel(OutSel_ABCD[8:6]));
  Multiplexer #(.select(3), .width(16)) multiplexer_4 (
    .in0(_0), .in1(_1), .in2(_2), .in3(_3), .in4(_4), .in5(_5), .in6(_6), .in7(_7), .out(A),
    .sel(OutSel_ABCD[11:9]));
endmodule

module ProcessorRegisters (
  input  \reg ,
  input  Jump,
  input  [6:0] Address,
  input  MemAdd,
  input  [15:0] MBRIn,
  input  [15:0] IRIn,
  input  [3:0] RegIn_PC_MAR_MBR_IR,
  input  [1:0] RegOut_MAR_MBR,
  output [6:0] MARout,
  output [15:0] MBRout,
  output [15:0] IRout
);

  wire [6:0] adder_1_out, MAR_q, multiplexer_1_out, multiplexer_2_out, PC_q;
  wire [15:0] MBR_q;

  Adder #(.width(7)) adder_1 (.a(PC_q), .b(7'b0000001), .out(adder_1_out));  // open: cin, cout
  Multiplexer #(.select(1), .width(7)) multiplexer_1 (
    .in0(adder_1_out), .in1(Address), .out(multiplexer_1_out), .sel(Jump));
  Register #(.width(7), .trigger("rising")) PC (
    .D(multiplexer_1_out), .Q(PC_q), .clk(RegIn_PC_MAR_MBR_IR[3]), .clr(\reg ));  // open: en
  Register #(.width(7), .trigger("rising")) MAR (
    .D(multiplexer_2_out), .Q(MAR_q), .clk(RegIn_PC_MAR_MBR_IR[2]), .clr(\reg ));  // open: en
  Multiplexer #(.select(1), .width(7)) multiplexer_2 (.in0(PC_q), .in1(Address), .out(multiplexer_2_out), .sel(MemAdd));
  Register #(.width(16), .trigger("rising")) MBR (
    .D(MBRIn), .Q(MBR_q), .clk(RegIn_PC_MAR_MBR_IR[1]), .clr(\reg ));  // open: en
  Register #(.width(16), .trigger("rising")) IR (
    .D(IRIn), .Q(IRout), .clk(RegIn_PC_MAR_MBR_IR[0]), .clr(\reg ));  // open: en
  assign MARout = RegOut_MAR_MBR[1] ? MAR_q : 7'bz;  // Controlled_Buffer controlled_buffer_1
  assign MBRout = RegOut_MAR_MBR[0] ? MBR_q : 16'bz;  // Controlled_Buffer controlled_buffer_2
endmodule

module ControlU (
  input  [15:0] ir,
  input  reset,
  input  clock,
  output regOut,
  output [6:0] address,
  output memAdd,
  output [3:0] PC_MAR_MBR_IR_in,
  output [1:0] MAR_MBR_out,
  output [11:0] ABCD,
  output MemRW,
  output sync,
  output [7:0] in_sE_sF,
  output ALUsum,
  output [1:0] AlUtoEF
);

  wire instdecoder_1_movm;
  wire [0:0] instdecoder_1_dir;
  wire [1:0] rom_1_data;
  wire [2:0] instdecoder_1_opcode, instdecoder_1_reg1;
  wire [3:3] or_1_out;
  wire [4:0] adder_1_out, multiplexer_1_out, register_1_q;
  wire [9:8] rom_1_data_2;

  or or_1 (or_1_out[3], instdecoder_1_dir[0], 1'b0);
  instDecoder instdecoder_1 (
    .movM(instdecoder_1_movm), .IRin(ir), .addressMEM(address), .opCode(instdecoder_1_opcode),
    .dir(instdecoder_1_dir[0]), .reg1(instdecoder_1_reg1), .reg2(in_sE_sF[2:0]));
  Adder #(.width(5)) adder_1 (.a(register_1_q), .b(5'b00001), .out(adder_1_out));  // open: cin, cout
  busSelector busselector_1 (
    .\reg (instdecoder_1_reg1), .dir(instdecoder_1_dir[0]), .MovM(instdecoder_1_movm), .ABCD(ABCD),
    .reg1(in_sE_sF[6:4]));
  Multiplexer #(.select(2), .width(5)) multiplexer_1 (
    .in0(adder_1_out), .in1({1'b1, or_1_out[3], instdecoder_1_opcode}), .in2({5{1'b0}}),
    .out(multiplexer_1_out), .sel(rom_1_data));  // open: in3
  Register #(.width(5), .trigger("rising")) register_1 (
    .D(multiplexer_1_out), .Q(register_1_q), .clk(clock), .clr(reset));  // open: en
  ROM #(.addrWidth(5), .dataWidth(16)) rom_1 (
    .addr(register_1_q),
    .data({PC_MAR_MBR_IR_in, MAR_MBR_out, rom_1_data_2, in_sE_sF[7], in_sE_sF[3], ALUsum, AlUtoEF[0], AlUtoEF[1], memAdd, rom_1_data}));  // open: sel
  memHiJacker memhijacker_1 (
    .dir(instdecoder_1_dir[0]), .movM(instdecoder_1_movm), .MRW(rom_1_data_2[9]), .MRW_2(MemRW));
  // Probe on in_sE_sF[7]
  // Probe on in_sE_sF[3]
  // Probe on AlUtoEF[0]
  // Probe on AlUtoEF[1]
  memHiJacker2 memhijacker2_1 (
    .dir(instdecoder_1_dir[0]), .Msync(rom_1_data_2[8]), .regOut(regOut), .Msync_2(sync));  // open: MRW, MRW_2

  // Notes on the sheet:
  //   contents of rom_1 (hex, n*v repeats v):
  //   4b00 9801 14*0 4 4b00 2700 482 4*0 4 4800 2c00 d02
endmodule

module instDecoder (
  input  [15:0] IRin,
  output [6:0] addressMEM,
  output movM,
  output [2:0] opCode,
  output dir,
  output [2:0] reg1,
  output [2:0] reg2
);

  wire decoder_1_out1, decoder_1_out2, decoder_1_out3;
  wire [1:0] controlled_buffer_1_out;
  wire [2:0] controlled_buffer_4_out;
  wire [6:0] controlled_buffer_2_out, controlled_buffer_3_out;

  Decoder #(.select(3), .tristate("false")) decoder_1 (
    .out0(movM), .out1(decoder_1_out1), .out2(decoder_1_out2), .out3(decoder_1_out3), .sel(IRin[15:13]));  // open: out4, out5, out6, out7
  assign {reg1, dir, addressMEM, controlled_buffer_1_out} = movM ? IRin[12:0] : 13'bz;  // Controlled_Buffer controlled_buffer_1
  assign {reg1, reg2, controlled_buffer_2_out} = decoder_1_out1 ? IRin[12:0] : 13'bz;  // Controlled_Buffer controlled_buffer_2
  assign {reg1, reg2, controlled_buffer_3_out} = decoder_1_out2 ? IRin[12:0] : 13'bz;  // Controlled_Buffer controlled_buffer_3
  assign {reg1, addressMEM, controlled_buffer_4_out} = decoder_1_out3 ? IRin[12:0] : 13'bz;  // Controlled_Buffer controlled_buffer_4

  assign opCode = IRin[15:13];
endmodule

module memHiJacker (
  input  dir,
  input  movM,
  input  MRW,
  output MRW_2
);

  wire not_1_out, or_1_out;

  or or_1 (or_1_out, movM, 1'b0);
  assign MRW_2 = or_1_out ? dir : 1'bz;  // Controlled_Buffer controlled_buffer_1
  not not_1 (not_1_out, or_1_out);
  assign MRW_2 = not_1_out ? MRW : 1'bz;  // Controlled_Buffer controlled_buffer_2
endmodule

module busSelector (
  input  [2:0] \reg ,
  input  dir,
  input  MovM,
  output [2:0] reg1,
  output [11:0] ABCD
);

  wire controlled_buffer_1_out, not_1_out;

  assign controlled_buffer_1_out = not_1_out ? 1'b0 : 1'bz;  // Controlled_Buffer controlled_buffer_1
  not not_1 (not_1_out, MovM);
  assign controlled_buffer_1_out = MovM ? dir : 1'bz;  // Controlled_Buffer controlled_buffer_2
  Demultiplexer #(.select(1), .width(3), .tristate("false")) demultiplexer_1 (
    .out0(reg1), .out1(ABCD[11:9]), .in(\reg ), .sel(controlled_buffer_1_out));

  // Notes on the sheet:
  //   1 registro a memoria
endmodule

module memHiJacker2 (
  input  dir,
  input  MRW,
  input  Msync,
  output regOut,
  output MRW_2,
  output Msync_2
);

  wire not_1_out;

  not not_1 (not_1_out, Msync);
  and and_1 (regOut, dir, not_1_out);

  assign MRW_2 = MRW;
  assign Msync_2 = Msync;
endmodule
